# Fritzing sketch OhaEnergyUseLog (saved by Fritzing 0.9.1b)
circuit board: 15.0696cm x 9.07427cm
breadboards: 1

parts:
  R1 = Resistor [tolerance=±5% resistance=33 package=THT]
  J1 = female pin header, 2 pins [form="♀ (female)"]
  R2 = Resistor [tolerance=±5% resistance=33 package=THT]
  J2 = female pin header, 2 pins [form="♀ (female)"]
  R3 = Resistor [tolerance=±5% resistance=33 package=THT]
  J3 = female pin header, 2 pins [form="♀ (female)"]
  D11 = Rectifier Diode [part_number=1N4001 package="300 mil [THT]"]
  D12 = Rectifier Diode [part_number=1N4001 package="300 mil [THT]"]
  D21 = Rectifier Diode [part_number=1N4001 package="300 mil [THT]"]
  D22 = Rectifier Diode [part_number=1N4001 package="300 mil [THT]"]
  D23 = Rectifier Diode [part_number=1N4001 package="300 mil [THT]"]
  D24 = Rectifier Diode [part_number=1N4001 package="300 mil [THT]"]
  D31 = Rectifier Diode [part_number=1N4001 package="300 mil [THT]"]
  D33 = Rectifier Diode [part_number=1N4001 package="300 mil [THT]"]
  D32 = Rectifier Diode [part_number=1N4001 package="300 mil [THT]"]
  D34 = Rectifier Diode [part_number=1N4001 package="300 mil [THT]"]
  D14 = Rectifier Diode [part_number=1N4001 package="300 mil [THT]"]
  D13 = Rectifier Diode [part_number=1N4001 package="300 mil [THT]"]
  Ams1117_3_3V = V_REG_LD1117VXX [package=78xxl]
  ESP8266-2 = female pin header, 4 pins [form="♀ (female)"]
  ESP8266-1 = female pin header, 4 pins [form="♀ (female)"]
  C-450uf = Electrolytic Capacitor [capacitance=1µF voltage=16V package="100 mil [THT, electrolytic]"]
  C-100uF = Electrolytic Capacitor [capacitance=1pF voltage=16V package="100 mil [THT, electrolytic]"]
  ESP8266_-_CL = Logic Level Converter
  Pad_-_GND = Pad [width=3.76752555555556 height=2.22464372277228 connect=center]
  RoboCore_-_BlackBoard_V1_0 = Arduino Uno (Rev3) - ICSP

nets:
  N1: R1.Pin_0, D11.cathode, D12.cathode, RoboCore_-_BlackBoard_V1_0.A0
  GND: R1.Pin_1, R2.Pin_1, R3.Pin_1, D23.anode, D24.anode, D33.anode, D34.anode, D14.anode, D13.anode, Ams1117_3_3V.GND, ESP8266-2.pin4, C-450uf.-, C-100uF.-, ESP8266_-_CL.GND, Pad_-_GND.pad, RoboCore_-_BlackBoard_V1_0.GND
  N2: J1.pin1, D11.anode, D13.cathode
  N3: J1.pin2, D12.anode, D14.cathode
  N4: R2.Pin_0, D21.cathode, D22.cathode, RoboCore_-_BlackBoard_V1_0.A1
  N5: J2.pin1, D21.anode, D23.cathode
  N6: J2.pin2, D22.anode, D24.cathode
  N7: R3.Pin_0, D31.cathode, D32.cathode, RoboCore_-_BlackBoard_V1_0.A2
  N8: J3.pin1, D31.anode, D33.cathode
  N9: J3.pin2, D32.anode, D34.cathode
  N10: Ams1117_3_3V.OUT, ESP8266-1.pin1, C-100uF.+, ESP8266_-_CL.LV
  N11: Ams1117_3_3V.IN, C-450uf.+, RoboCore_-_BlackBoard_V1_0.VIN
  N12: ESP8266-2.pin1, ESP8266_-_CL.RX_LV
  N13: ESP8266-1.pin3, ESP8266_-_CL.RX2_LV
  N14: ESP8266-1.pin4, ESP8266_-_CL.TX_LV
  N15: ESP8266_-_CL.TX_HV, RoboCore_-_BlackBoard_V1_0.D2
  N16: ESP8266_-_CL.RX_HV, RoboCore_-_BlackBoard_V1_0.D3_PWM
  N17: ESP8266_-_CL.HV, RoboCore_-_BlackBoard_V1_0.5V
  N18: ESP8266_-_CL.RX2_HV, RoboCore_-_BlackBoard_V1_0.D4

notes:
  OHA 1.0 24/06/16

custom parts:
  Logic Level Converter: Description: If you've ever tried to connect a 3.3V device to a 5V system, you know what a challenge it can be. The SparkFun logic level converter is a small device that safely steps down 5V signals to 3.3V and steps up 3.3V to 5V. This level converter also works with 2.8V and 1.8V devices. Each level converter has the capability of converting 4 pins on the high side to 4 pins on the low side.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
